// Logisim project Processador_8bit_Spike_T16.circ as structural Verilog: 1 circuit, main circuit Processador8bitSpike
module Processador8bitSpike (
  output [7:0] out_1
);

  wire button_1_out, clock_1_out;
  wire [7:0] adder_1_out, adder_2_out, bit_extender_1_out, multiplexer_1_out, multiplexer_2_out,
       multiplexer_3_out, multiplexer_4_out, negator_1_out, register_1_q, rom_1_data, subtractor_1_out;

  Adder adder_1 (.a(register_1_q), .b({8{1'b0}}), .out(adder_1_out), .cin(1'b1));  // open: cout
  Register register_1 (.D(adder_1_out), .en(1'b1), .clk(clock_1_out), .Q(register_1_q), .clr(button_1_out));
  ROM rom_1 (.addr(register_1_q), .data(rom_1_data));
  assign bit_extender_1_out = {{2{1'b0}}, rom_1_data[5:0]};  // Bit_Extender bit_extender_1
  Button button_1 (.out(button_1_out));
  Clock clock_1 (.out(clock_1_out));
  Adder adder_2 (.a(out_1), .b(bit_extender_1_out), .out(adder_2_out));  // open: cin, cout
  Subtractor subtractor_1 (.a(out_1), .b(bit_extender_1_out), .out(subtractor_1_out));  // open: bin, bout
  Multiplexer #(.width(8)) multiplexer_1 (.in0(out_1), .in1({8{1'b0}}), .out(multiplexer_1_out), .sel(out_1[7]));
  Multiplexer #(.width(8)) multiplexer_2 (.in0(out_1), .in1(negator_1_out), .out(multiplexer_2_out), .sel(out_1[7]));
  Negator negator_1 (.in(out_1), .out(negator_1_out));
  Multiplexer #(.width(8)) multiplexer_3 (
    .in0(multiplexer_1_out), .in1(multiplexer_2_out), .out(multiplexer_3_out), .sel(rom_1_data[5]));
  Multiplexer #(.select(2), .width(8)) multiplexer_4 (
    .in0(adder_2_out), .in1(subtractor_1_out), .in2(multiplexer_3_out), .in3(bit_extender_1_out),
    .out(multiplexer_4_out), .sel(rom_1_data[7:6]));
  Register register_2 (.D(multiplexer_4_out), .en(1'b1), .clk(clock_1_out), .Q(out_1), .clr(button_1_out));

  // Notes on the sheet:
  //   contents of rom_1 (hex, n*v repeats v):
  //   76*0 21
endmodule
